// Digital circuit RV32I-Fetch-Control.dig as structural Verilog
module RV32I_Fetch_Control (
  input  Normal,
  input  Run,
  input  Go,
  output PC_Enable,
  output Memory_Store,
  output PC_Incrementer_Set_PC
);

  not not_1 (Memory_Store, Normal);

  assign PC_Enable = Run;
  assign PC_Incrementer_Set_PC = Normal;
endmodule
