// Digital circuit RV32I.dig as structural Verilog
module RV32I (
  input  CLC
);

  wire ALU_INSTR, ALU_SET_MEM_R_W_A, ALU_SET_PC, ALU_SET_REGISTER, BOOT_CNT_EN, BOOT_CNT_SET_MEM_R_W_A,
       BOOT_COMPLETE, BOOT_COUNTER_OVERFLOW, CLC_t, DECODE_BRANCH_HOLD, ERROR, EXECUTE_BRANCH_HOLD, GO,
       INSTR_DECODE_EN, INSTR_EXECUTE_EN, INSTR_MEMORY_EN, MEM_STR, NORMAL, not_1_out, not_2_out, not_3_out,
       or_1_out, P_out, PC_EN, PC_INC_SET_PC, PC_STALL, R_out, REGISTER_HOLD, RESERVE, ROM_SET_MEM_R_W, RUN,
       S_out, SET_ERROR, T_out;
  wire [2:2] rv32i_instruction_decoder_1_p4;
  wire [4:0] RS1_A, RS2_A, rv32i_register_reserve_1_e, rv32i_register_reserve_1_o;
  wire [23:0] driver_8_out, MEM_R_W_A, PC_EXECUTE, PC_IN, PC_INC_OUT, PC_OUT, ROM_A;
  wire [31:0] driver_6_out, driver_7_out, EXECUTE_RESULT, INSTR_DECODE, INSTR_EXECUTE, INSTR_MEMORY,
       INSTR_WRITE, MEM_R_W, MEMORY_RESULT, RESULT_q, ROM, RS1, RS2, rv32i_alu_input_1_a, rv32i_alu_input_1_b;
  wire [31:24] driver_10_out, driver_11_out;

  not not_1 (not_1_out, ERROR);
  assign CLC_t = not_1_out ? CLC : 1'bz;  // Driver driver_1
  Button R (.out(R_out));
  or or_1 (or_1_out, REGISTER_HOLD, 1'b0, EXECUTE_BRANCH_HOLD, DECODE_BRANCH_HOLD);
  Button S (.out(S_out));
  Button T (.out(T_out));
  Counter #(.Bits(24)) BOOT_CNT (.en(BOOT_CNT_EN), .C(CLC_t), .clr(NORMAL), .out(ROM_A), .ovf(BOOT_COUNTER_OVERFLOW));
  Button P (.out(P_out));
  RV32I_Control rv32i_control_1 (
    .START(S_out), .PAUSE(P_out), .RESET(R_out), .HOLD(or_1_out), .SET_ERROR(SET_ERROR), .BC(BOOT_COMPLETE),
    .BCO(BOOT_COUNTER_OVERFLOW), .CLC(CLC_t), .RUN_OVERRIDE(T_out), .NORMAL(NORMAL), .RUN(RUN), .GO(GO),
    .ERROR(ERROR), .BCE(BOOT_CNT_EN), .BC_SET_R_W_A(BOOT_CNT_SET_MEM_R_W_A), .ROM_SET_MEM_R_W(ROM_SET_MEM_R_W));
  assign MEM_R_W_A = BOOT_CNT_SET_MEM_R_W_A ? ROM_A : 24'bz;  // Driver driver_2
  ROM #(.AddrBits(24), .isProgramMemory("true"), .Bits(32)) u_ROM (.A(ROM_A), .sel(1'b1), .D(ROM));
  Comparator #(.Bits(24)) comparator_1 (.a(ROM_A), .b(24'h19), .eq(BOOT_COMPLETE));  // open: gt, lt
  Seven_Seg_Hex seven_seg_hex_1 (.d(ROM[31:28]), .dp(1'b0));
  Seven_Seg_Hex seven_seg_hex_2 (.d(ROM_A[23:20]), .dp(1'b0));
  Seven_Seg_Hex seven_seg_hex_3 (.d(ROM[27:24]), .dp(1'b0));
  Seven_Seg_Hex seven_seg_hex_4 (.d(ROM[23:20]), .dp(1'b0));
  Seven_Seg_Hex seven_seg_hex_5 (.d(ROM_A[19:16]), .dp(1'b0));
  Seven_Seg_Hex seven_seg_hex_6 (.d(ROM_A[15:12]), .dp(1'b0));
  Seven_Seg_Hex seven_seg_hex_7 (.d(ROM[19:16]), .dp(1'b0));
  Seven_Seg_Hex seven_seg_hex_8 (.d(ROM[15:12]), .dp(1'b0));
  assign PC_IN = PC_STALL ? PC_OUT : 24'bz;  // Driver driver_3
  Seven_Seg_Hex seven_seg_hex_9 (.d(ROM_A[11:8]), .dp(1'b0));
  Seven_Seg_Hex seven_seg_hex_10 (.d(ROM_A[7:4]), .dp(1'b0));
  Seven_Seg_Hex seven_seg_hex_11 (.d(ROM[11:8]), .dp(1'b0));
  Seven_Seg_Hex seven_seg_hex_12 (.d(ROM[7:4]), .dp(1'b0));
  Register #(.Bits(24), .isProgramCounter("true")) PC (.D(PC_IN), .C(CLC_t), .en(PC_EN), .Q(PC_OUT));
  Add #(.Bits(24)) PC_INC (.a(PC_OUT), .b(24'h1), .c_i(1'b0), .s(PC_INC_OUT));  // open: c_o
  RV32I_Fetch_Control rv32i_fetch_control_1 (
    .Normal(NORMAL), .Run(RUN), .Go(GO), .ALU_SET_PC(ALU_SET_PC), .PC_EN(PC_EN), .Memory_Store(MEM_STR),
    .PC_Incrementer_Set_PC(PC_INC_SET_PC), .PC_STALL(PC_STALL));
  Seven_Seg_Hex seven_seg_hex_13 (.d(ROM_A[3:0]), .dp(1'b0));
  Seven_Seg_Hex seven_seg_hex_14 (.d(ROM[3:0]), .dp(1'b0));
  assign PC_IN = PC_INC_SET_PC ? PC_INC_OUT : 24'bz;  // Driver driver_4
  PullDown #(.Bits(24)) pulldown_1 (.out(PC_IN));
  Seven_Seg_Hex seven_seg_hex_15 (.d(MEM_R_W[31:28]), .dp(1'b0));
  Seven_Seg_Hex seven_seg_hex_16 (.d(MEM_R_W_A[23:20]), .dp(1'b0));
  Seven_Seg_Hex seven_seg_hex_17 (.d(MEM_R_W[27:24]), .dp(1'b0));
  Seven_Seg_Hex seven_seg_hex_18 (.d(MEM_R_W[23:20]), .dp(1'b0));
  not not_2 (not_2_out, MEM_STR);
  PullDown #(.Bits(24)) pulldown_2 (.out(MEM_R_W_A));
  Seven_Seg_Hex seven_seg_hex_19 (.d(MEM_R_W_A[19:16]), .dp(1'b0));
  Seven_Seg_Hex seven_seg_hex_20 (.d(MEM_R_W_A[15:12]), .dp(1'b0));
  Seven_Seg_Hex seven_seg_hex_21 (.d(MEM_R_W[19:16]), .dp(1'b0));
  Seven_Seg_Hex seven_seg_hex_22 (.d(MEM_R_W[15:12]), .dp(1'b0));
  RAMDualAccess #(.AddrBits(24), .Bits(32)) Memory (
    .str(MEM_STR), .C(CLC_t), .ld(not_2_out), .A1(MEM_R_W_A), .Din1(MEM_R_W), .A2(PC_OUT), .D1(MEM_R_W),
    .D2(INSTR_DECODE));
  Seven_Seg_Hex seven_seg_hex_23 (.d(MEM_R_W_A[11:8]), .dp(1'b0));
  Seven_Seg_Hex seven_seg_hex_24 (.d(MEM_R_W_A[7:4]), .dp(1'b0));
  Seven_Seg_Hex seven_seg_hex_25 (.d(MEM_R_W[11:8]), .dp(1'b0));
  Seven_Seg_Hex seven_seg_hex_26 (.d(MEM_R_W[7:4]), .dp(1'b0));
  assign MEM_R_W = ROM_SET_MEM_R_W ? ROM : 32'bz;  // Driver driver_5
  Seven_Seg_Hex seven_seg_hex_27 (.d(MEM_R_W_A[3:0]), .dp(1'b0));
  Seven_Seg_Hex seven_seg_hex_28 (.d(MEM_R_W[3:0]), .dp(1'b0));
  Seven_Seg_Hex seven_seg_hex_29 (.d(INSTR_DECODE[31:28]), .dp(1'b0));
  Seven_Seg_Hex seven_seg_hex_30 (.d(PC_OUT[23:20]), .dp(1'b0));
  Seven_Seg_Hex seven_seg_hex_31 (.d(INSTR_DECODE[27:24]), .dp(1'b0));
  Seven_Seg_Hex seven_seg_hex_32 (.d(INSTR_DECODE[23:20]), .dp(1'b0));
  Seven_Seg_Hex seven_seg_hex_33 (.d(PC_OUT[19:16]), .dp(1'b0));
  Seven_Seg_Hex seven_seg_hex_34 (.d(PC_OUT[15:12]), .dp(1'b0));
  Seven_Seg_Hex seven_seg_hex_35 (.d(INSTR_DECODE[19:16]), .dp(1'b0));
  Seven_Seg_Hex seven_seg_hex_36 (.d(INSTR_DECODE[15:12]), .dp(1'b0));
  Seven_Seg_Hex seven_seg_hex_37 (.d(PC_OUT[11:8]), .dp(1'b0));
  Seven_Seg_Hex seven_seg_hex_38 (.d(PC_OUT[7:4]), .dp(1'b0));
  Seven_Seg_Hex seven_seg_hex_39 (.d(INSTR_DECODE[11:8]), .dp(1'b0));
  Seven_Seg_Hex seven_seg_hex_40 (.d(INSTR_DECODE[7:4]), .dp(1'b0));
  Seven_Seg_Hex seven_seg_hex_41 (.d(PC_OUT[3:0]), .dp(1'b0));
  Seven_Seg_Hex seven_seg_hex_42 (.d(INSTR_DECODE[3:0]), .dp(1'b0));
  Seven_Seg_Hex seven_seg_hex_43 (.d(INSTR_EXECUTE[31:28]), .dp(1'b0));
  Seven_Seg_Hex seven_seg_hex_44 (.d(INSTR_EXECUTE[27:24]), .dp(1'b0));
  Seven_Seg_Hex seven_seg_hex_45 (.d(INSTR_EXECUTE[23:20]), .dp(1'b0));
  assign driver_6_out = RESERVE ? INSTR_DECODE : 32'bz;  // Driver driver_6
  RV32I_Decode_Control rv32i_decode_control_1 (
    .INSTR(INSTR_DECODE), .Normal(NORMAL), .Run(RUN), .Go(GO), .DECODE_HOLD(DECODE_BRANCH_HOLD),
    .DECODE_EN(INSTR_DECODE_EN), .RESERVE(RESERVE), .ERROR(SET_ERROR));
  Seven_Seg_Hex seven_seg_hex_46 (.d(INSTR_EXECUTE[19:16]), .dp(1'b0));
  Seven_Seg_Hex seven_seg_hex_47 (.d(INSTR_EXECUTE[15:12]), .dp(1'b0));
  assign driver_7_out = GO ? INSTR_DECODE : 32'bz;  // Driver driver_7
  PullDown #(.Bits(32)) pulldown_3 (.out(driver_7_out));
  assign driver_8_out = GO ? PC_OUT : 24'bz;  // Driver driver_8
  PullDown #(.Bits(24)) pulldown_4 (.out(driver_8_out));
  PullDown #(.Bits(32)) pulldown_5 (.out(driver_6_out));
  not not_3 (not_3_out, PC_OUT[0]);
  Seven_Seg_Hex seven_seg_hex_48 (.d(INSTR_EXECUTE[11:8]), .dp(1'b0));
  Seven_Seg_Hex seven_seg_hex_49 (.d(INSTR_EXECUTE[7:4]), .dp(1'b0));
  Register #(.Bits(32)) INSTR (.D(driver_7_out), .C(CLC_t), .en(INSTR_DECODE_EN), .Q(INSTR_EXECUTE));
  Register #(.Bits(24)) PC_2 (.D(driver_8_out), .C(CLC_t), .en(INSTR_DECODE_EN), .Q(PC_EXECUTE));
  RV32I_Register_Reserve rv32i_register_reserve_1 (
    .INSTR(driver_6_out), .CLC(CLC_t), .RE(not_3_out), .RO(PC_OUT[0]), .HOLD(REGISTER_HOLD),
    .E(rv32i_register_reserve_1_e), .O(rv32i_register_reserve_1_o));
  Seven_Seg_Hex seven_seg_hex_50 (.d(INSTR_EXECUTE[3:0]), .dp(1'b0));
  Seven_Seg_Hex seven_seg_hex_51 (.d(INSTR_MEMORY[31:28]), .dp(1'b0));
  Seven_Seg_Hex seven_seg_hex_52 (.d(INSTR_MEMORY[27:24]), .dp(1'b0));
  Seven_Seg_Hex seven_seg_hex_53 (.d(INSTR_MEMORY[23:20]), .dp(1'b0));
  PullDown pulldown_6 (.out(REGISTER_HOLD));
  Seven_Seg_Hex seven_seg_hex_54 (.d(INSTR_MEMORY[19:16]), .dp(1'b0));
  Seven_Seg_Hex seven_seg_hex_55 (.d(INSTR_MEMORY[15:12]), .dp(1'b0));
  Seven_Seg_Hex seven_seg_hex_56 (.d(INSTR_MEMORY[11:8]), .dp(1'b0));
  Seven_Seg_Hex seven_seg_hex_57 (.d(INSTR_MEMORY[7:4]), .dp(1'b0));
  Seven_Seg_Hex seven_seg_hex_58 (.d(INSTR_MEMORY[3:0]), .dp(1'b0));
  Seven_Seg_Hex seven_seg_hex_59 (.d(INSTR_WRITE[31:28]), .dp(1'b0));
  Seven_Seg_Hex seven_seg_hex_60 (.d(INSTR_WRITE[27:24]), .dp(1'b0));
  Seven_Seg_Hex seven_seg_hex_61 (.d(INSTR_WRITE[23:20]), .dp(1'b0));
  RV32I_ALU_Input rv32i_alu_input_1 (
    .INSTR(INSTR_EXECUTE), .PC(PC_EXECUTE), .RS1(RS1), .RS2(RS2), .A(rv32i_alu_input_1_a),
    .B(rv32i_alu_input_1_b));  // open: COMP_A, COMP_B
  Seven_Seg_Hex seven_seg_hex_62 (.d(INSTR_WRITE[19:16]), .dp(1'b0));
  Seven_Seg_Hex seven_seg_hex_63 (.d(INSTR_WRITE[15:12]), .dp(1'b0));
  // RV32I_Execute_Control rv32i_execute_control_1: pin names not known; wires that end beside it: INSTR_EXECUTE, NORMAL, RUN, GO, EXECUTE_BRANCH_HOLD, INSTR_EXECUTE_EN, ALU_INSTR, RS1_A, RS2_A
  Seven_Seg_Hex seven_seg_hex_64 (.d(INSTR_WRITE[11:8]), .dp(1'b0));
  Seven_Seg_Hex seven_seg_hex_65 (.d(INSTR_WRITE[7:4]), .dp(1'b0));
  Register #(.Bits(32)) INSTR_2 (.D(INSTR_EXECUTE), .C(CLC_t), .en(INSTR_EXECUTE_EN), .Q(INSTR_MEMORY));
  // RV32I_ALU ALU: pin names not known; wires that end beside it: rv32i_alu_input_1_a, rv32i_alu_input_1_b, ALU_INSTR, EXECUTE_RESULT
  Seven_Seg_Hex seven_seg_hex_66 (.d(INSTR_WRITE[3:0]), .dp(1'b0));
  Register #(.Bits(32)) INSTR_3 (.D(INSTR_MEMORY), .C(CLC_t), .en(INSTR_MEMORY_EN), .Q(INSTR_WRITE));
  Register #(.Bits(32)) RESULT (.D(EXECUTE_RESULT), .C(CLC_t), .en(1'b1), .Q(RESULT_q));
  // RV32I_Instruction_Decoder rv32i_instruction_decoder_1: pin names not known; wires that end beside it: RUN, GO, INSTR_MEMORY, {rv32i_instruction_decoder_1_p4[2], ALU_SET_PC, ALU_SET_REGISTER}
  and and_1 (INSTR_MEMORY_EN, NORMAL, RUN);
  assign MEMORY_RESULT = ALU_SET_REGISTER ? RESULT_q : 32'bz;  // Driver driver_9
  assign {driver_10_out, PC_IN} = ALU_SET_PC ? RESULT_q : 32'bz;  // Driver driver_10
  assign {driver_11_out, MEM_R_W_A} = ALU_SET_MEM_R_W_A ? RESULT_q : 32'bz;  // Driver driver_11
  and and_2 (ALU_SET_MEM_R_W_A, rv32i_instruction_decoder_1_p4[2], NORMAL);
  RegisterFile #(.AddrBits(5), .Bits(32)) registerfile_1 (
    .Din(MEMORY_RESULT), .we(1'b0), .Rw(INSTR_WRITE[11:7]), .C(CLC_t), .Ra(RS1_A), .Rb(RS2_A), .Da(RS1),
    .Db(RS2));

  // Notes on the sheet:
  //   CLC: Hz: 20
  //   PROGRAM LENGTH
  //   contents of ROM (hex, n*v repeats v):
  //   140006f,aaaaaaaa,0,0,0,0,0,0,0,0,0,0,0,0,0,0,0,0,0,0,1437,497,80848533,809405b3,b57633,
  //   b566b3,b54733,1341793,c55813,c5d893,fff7c913,ffb97993,57ea13,8a1ab3,8a5b33,808a5bb3,
  //   17b2c33,16bacb3,17b3d33,16bbdb3,bae13,b2e93,bbf13,243f93,100103,4010123,6011123,104103,
  //   8010123,a011123,101103,c011123,e012123,105103,10011123,12012123,13,fffff06f
  //   ROM
  //   MEM R/W
  //   INSTR
  //   EXECUTE
  //   MEMORY
  //   WRITE
endmodule
